// Logisim project BPU.circ as structural Verilog: 12 circuits, main circuit main
module main (
  input  C0,
  input  C1,
  input  C2,
  input  T0,
  input  T1,
  input  T2,
  output MEM__D
);

  wire AND_2_out, AND_out, not_1_out, not_2_out;

  not not_1 (not_1_out, C0);
  not not_2 (not_2_out, C1);
  and AND (AND_out, T1, not_2_out, not_1_out);
  and AND_2 (AND_2_out, T1, C2, C1, C0);
  or OR (MEM__D, AND_out, T0, AND_2_out);

  // Notes on the sheet:
  //   Command
  //   Time
endmodule

module BPU_Layout (
  input  [7:0] Data_In,
  output [7:0] Address_Out,
  output [7:0] Data_Out
);


  assign Address_Out = Data_In;
  assign Data_Out = Data_In;

  // Notes on the sheet:
  //   Data
  //   Pointer
  //   Program
  //   Counter
  //   Arithmetic and Logic
  //   Unit
  //   Program
  //   Register
  //   Command
  //   decoder
endmodule

module BPU (
  input  _0,
  input  [7:0] Data_In,
  input  Clock,
  input  Reset,
  input  Load,
  input  D__DP,
  input  DP__D,
  input  D__ALU,
  input  DP__A,
  input  NEG,
  input  [4:0] Argument,
  input  ALU__D,
  input  NEG_2,
  input  _0_2,
  input  D__PR,
  input  D__PC,
  input  PC_plus_plus,
  input  PC__D,
  input  PC__A,
  input  Load_from_ROM,
  output [7:0] Address_Out,
  output MEM__D,
  output D__MEM,
  output [7:0] Data_Out,
  output [4:0] I_O_argument,
  output I_O,
  output Direction_select
);

  wire AND_out, clock_1_out, clock_2_out, clock_3_out, clock_4_out, clock_5_out, Reset_2_out, Reset_3_out,
       Reset_out, XOR_out;
  wire [7:0] alu_1_data_2, counter_1_q, register_1_q, register_2_q;

  assign Address_Out = DP__A ? register_1_q : 8'bz;  // Controlled_Buffer controlled_buffer_1
  Clock clock_1 (.out(clock_1_out));
  and AND (AND_out, XOR_out, D__PC);
  assign Address_Out = PC__A ? counter_1_q : 8'bz;  // Controlled_Buffer controlled_buffer_2
  Clock clock_2 (.out(clock_2_out));
  assign Data_In = DP__D ? register_1_q : 8'bz;  // Controlled_Buffer controlled_buffer_3
  Register register_1 (.D(Data_In), .en(D__DP), .Q(register_1_q), .clk(clock_1_out), .clr(Reset_out));
  Button u_Reset (.out(Reset_out));
  xor XOR (XOR_out, NEG_2, _0_2);
  Counter counter_1 (
    .load(AND_out), .D(Data_In), .count(PC_plus_plus), .Q(counter_1_q), .clk(clock_2_out), .clr(Reset_2_out));  // open: carry
  assign Data_In = PC__D ? counter_1_q : 8'bz;  // Controlled_Buffer controlled_buffer_4
  Button Reset_2 (.out(Reset_2_out));
  Clock clock_3 (.out(clock_3_out));
  Clock clock_4 (.out(clock_4_out));
  assign Data_In = ALU__D ? alu_1_data_2 : 8'bz;  // Controlled_Buffer controlled_buffer_5
  ALU alu_1 (
    .Argument(Argument), .Data(Data_In), .D__ALU(D__ALU), .Clock(clock_4_out), .Data_2(alu_1_data_2),
    .NEG(NEG));
  // Probe on register_2_q[7:3]
  Register register_2 (.D(Data_In), .en(D__PR), .Q(register_2_q), .clk(clock_3_out));  // open: clr
  // Probe on register_2_q[2:0]
  // Probe on register_2_q[0]
  Command_Decoder command_decoder_1 (
    .Command(register_2_q[2:0]), .Clock(clock_5_out), .Reset(Reset_3_out), .Load(Load_from_ROM));  // open: D__PR, ALU__D, D__MEM, MEM__D, D__DP, DP__D, DP__A, D__PC, PC_plus_plus, PC__A, PC__D, I_O
  Clock clock_5 (.out(clock_5_out));
  Button Reset_3 (.out(Reset_3_out));

  assign Data_Out = Data_In;
endmodule

module Command_Decoder (
  input  [2:0] Command,
  input  Clock,
  input  Reset,
  input  Load,
  output D__PR,
  output ALU__D,
  output D__MEM,
  output MEM__D,
  output I_O,
  output D__DP,
  output DP__D,
  output DP__A,
  output D__PC,
  output PC__D,
  output PC_plus_plus,
  output PC__A
);

  wire AND_2_out, AND_3_out, AND_4_out, AND_5_out, AND_out, not_1_out, not_2_out, not_3_out, OR_out,
       shift_register_1_q0;

  not not_1 (not_1_out, Command[2]);
  not not_2 (not_2_out, Command[1]);
  not not_3 (not_3_out, Clock);
  nor NOR (D__PR, shift_register_1_q0, Load, ALU__D);
  Shift_Register #(.length(2)) shift_register_1 (
    .shift(1'b1), .in(D__PR), .clk(not_3_out), .clr(OR_out), .q0(shift_register_1_q0), .q1(ALU__D));  // open: out, load, d0, d1
  or OR (OR_out, Reset, AND_out, Load);
  and AND (AND_out, ALU__D, Command[1], Command[2]);
  and AND_2 (AND_2_out, not_2_out, not_1_out);
  and AND_3 (AND_3_out, Command[1], Command[2]);
  and AND_4 (AND_4_out, shift_register_1_q0, not_2_out, not_1_out);
  and AND_5 (AND_5_out, ALU__D, Command[0], Command[1], Command[2]);
  and AND_6 (I_O, shift_register_1_q0, Command[1], Command[2]);
  and AND_7 (D__DP, ALU__D, Command[1]);
  and AND_8 (DP__D, shift_register_1_q0, Command[1], not_1_out);
  or OR_2 (DP__A, ALU__D, shift_register_1_q0);
  and AND_9 (D__PC, ALU__D, Command[2]);
  and AND_10 (PC__D, shift_register_1_q0, not_2_out, Command[2]);
  or OR_3 (PC__A, Load, D__PR);
  or OR_4 (D__MEM, AND_2_out, Load, AND_3_out);
  or OR_5 (MEM__D, AND_4_out, D__PR, AND_5_out);

  assign PC_plus_plus = PC__A;
endmodule

module ALU (
  input  [4:0] Argument,
  input  [7:0] Data,
  input  D__ALU,
  input  Clock,
  input  NEG,
  output [7:0] Data_2
);

  wire [7:0] adder_1_out, register_1_q, XOR_out;

  Register register_1 (.D(Data), .en(D__ALU), .Q(register_1_q), .clk(Clock));  // open: clr
  assign XOR_out = {8{NEG}} ^ register_1_q;  // XOR_Gate XOR, 8 bits wide
  Adder adder_1 (.a({3'b000, Argument}), .b(XOR_out), .out(adder_1_out), .cin(1'b1));  // open: cout
  assign Data_2 = adder_1_out ^ {8{NEG}};  // XOR_Gate XOR_2, 8 bits wide
endmodule

module Display_driver (
  input  [7:0] Data_in,
  input  Reset,
  input  Clock,
  input  Enable,
  output [3:0] High_nibble,
  output [3:0] Low_nibble,
  output Ready
);

  wire not_1_out;

  not not_1 (not_1_out, Enable);
  Register register_1 (.D(Data_in), .en(Enable), .Q({High_nibble, Low_nibble}), .clk(Clock), .clr(Reset));
  D_Flip_Flop d_ff_1 (.clk(Clock), .D(Enable), .Q(Ready), .preset(1'b0), .en(1'b1), .reset(not_1_out));  // open: Qn
endmodule

module _0_Flag (
  input  [7:0] Data,
  output Is_zero
);

  nor NOR (Is_zero, Data[0], Data[1], Data[2], Data[3], Data[5], Data[6], Data[7], Data[4]);
endmodule

module Load_signal_generator (
  input  Clock,
  input  [7:0] Adress_bus,
  input  Reset,
  output Load
);

  wire nor_1_out, not_1_out;

  not not_1 (not_1_out, Clock);
  nor nor_1 (nor_1_out, Adress_bus[0], Adress_bus[1], Adress_bus[2], Adress_bus[3], Adress_bus[5], Adress_bus[6], Adress_bus[7], Adress_bus[4]);
  S_R_Flip_Flop s_r_ff_1 (
    .S(1'b0), .clk(not_1_out), .R(nor_1_out), .Q(Load), .preset(Reset), .en(1'b1));  // open: Qn, reset
endmodule

module Simple_showcases (
  input  [7:0] B,
  input  in,
  input  [7:0] Address_bus,
  input  [7:0] A,
  input  NEG,
  input  [7:0] Input,
  input  Reset,
  input  Clock,
  input  Next_Command,
  input  [7:0] Data_bus,
  input  Halt,
  input  Clock_2,
  input  Reset_2,
  input  Resume,
  input  D__ALU,
  input  NEG_2,
  input  Load,
  input  [4:0] Argument,
  input  ALU__D,
  input  Wait,
  output [7:0] A_____B,
  output out_22,
  output BPU_clock,
  output _0,
  output _1,
  output _2,
  output L
);

  wire clock_1_out, clock_2_out, Confirm_out, load_signal_generator_1_load, not_1_out, not_2_out, not_3_out,
       OR_2_out, OR_out;
  wire [7:0] adder_1_out, alu_1_data_2, controlled_buffer_1_out, rom_1_data, XOR_out;

  Clock clock_1 (.out(clock_1_out));
  Load_signal_generator load_signal_generator_1 (
    .Clock(clock_1_out), .Adress_bus(Address_bus), .Reset(Reset), .Load(load_signal_generator_1_load));
  not not_1 (not_1_out, Wait);
  not not_2 (not_2_out, Halt);
  or OR (OR_out, Resume, not_1_out);
  ROM rom_1 (.addr(Address_bus), .data(rom_1_data), .sel(load_signal_generator_1_load));
  // Probe on rom_1_data
  // Probe on load_signal_generator_1_load
  and AND (BPU_clock, Clock, not_2_out, OR_out);
  LED Input_request (.in(in));
  assign controlled_buffer_1_out = in ? Input : 8'bz;  // Controlled_Buffer controlled_buffer_1
  Button Confirm (.out(Confirm_out));
  Clock u_clock_2 (.out(clock_2_out));
  // Probe on controlled_buffer_1_out
  assign Data_bus = ALU__D ? alu_1_data_2 : 8'bz;  // Controlled_Buffer controlled_buffer_2
  // Probe on alu_1_data_2
  ALU alu_1 (
    .Argument(Argument), .Data(Data_bus), .D__ALU(D__ALU), .Clock(clock_2_out), .Data_2(alu_1_data_2),
    .NEG(NEG_2));
  // Probe on Confirm_out
  not not_3 (not_3_out, Clock_2);
  nor NOR (_0, _1, Load, _2);
  assign XOR_out = A ^ {8{NEG}};  // XOR_Gate XOR, 8 bits wide
  Shift_Register #(.length(2)) shift_register_1 (
    .shift(1'b1), .in(_0), .clk(not_3_out), .clr(OR_2_out), .q0(_1), .q1(_2));  // open: out, load, d0, d1
  Adder adder_1 (.a(B), .b(XOR_out), .out(adder_1_out));  // open: cin, cout
  or OR_2 (OR_2_out, Next_Command, Reset_2, Load);
  assign A_____B = adder_1_out ^ {8{NEG}};  // XOR_Gate XOR_2, 8 bits wide

  assign L = Load;

  // Notes on the sheet:
  //   ROM
  //   Clock logic
  //   Input
  //   ALU
  //   Add/subtract
  //   Cycle Counter
endmodule

module Register_showcases (
  input  D__DP,
  input  [7:0] Data_bus,
  input  DP__D,
  input  D__PR,
  input  DP__A,
  input  NEG,
  input  _0,
  input  D__PC,
  input  PC_plus_plus,
  input  PC__D,
  input  PC__A
);

  wire AND_out, clock_1_out, clock_2_out, clock_3_out, Reset_2_out, Reset_out, XOR_out;
  wire [7:0] controlled_buffer_1_out, controlled_buffer_2_out, controlled_buffer_3_out,
       controlled_buffer_4_out, counter_1_q, register_1_q, register_2_q;

  // Probe on controlled_buffer_1_out
  assign controlled_buffer_1_out = DP__A ? register_1_q : 8'bz;  // Controlled_Buffer controlled_buffer_1
  Register register_1 (.D(controlled_buffer_2_out), .en(D__DP), .Q(register_1_q), .clk(clock_1_out), .clr(Reset_out));
  Button Reset (.out(Reset_out));
  Clock clock_1 (.out(clock_1_out));
  xor XOR (XOR_out, NEG, _0);
  // Probe on controlled_buffer_3_out
  assign controlled_buffer_2_out = DP__D ? register_1_q : 8'bz;  // Controlled_Buffer controlled_buffer_2
  // Probe on controlled_buffer_2_out
  and AND (AND_out, XOR_out, D__PC);
  assign controlled_buffer_3_out = PC__A ? counter_1_q : 8'bz;  // Controlled_Buffer controlled_buffer_3
  Clock clock_2 (.out(clock_2_out));
  Counter counter_1 (
    .load(AND_out), .D(controlled_buffer_4_out), .count(PC_plus_plus), .Q(counter_1_q), .clk(clock_2_out),
    .clr(Reset_2_out));  // open: carry
  // Probe on controlled_buffer_4_out
  assign controlled_buffer_4_out = PC__D ? counter_1_q : 8'bz;  // Controlled_Buffer controlled_buffer_4
  Button Reset_2 (.out(Reset_2_out));
  Clock clock_3 (.out(clock_3_out));
  // Probe on register_2_q[7:3]
  Register register_2 (.D(Data_bus), .en(D__PR), .Q(register_2_q), .clk(clock_3_out));  // open: clr
  // Probe on register_2_q[0]
  // Probe on register_2_q[2:0]

  // Notes on the sheet:
  //   Data pointer
  //   Program counter
  //   Program register
endmodule

module RAM_showcase (
  input  [7:0] Address_bus,
  input  MEM__D,
  input  D__MEM
);

  wire clock_1_out, n0_flag_1_is_zero, Reset_out;
  wire [7:0] controlled_buffer_1_out, ram_1_data;

  Clock clock_1 (.out(clock_1_out));
  RAM #(.bus("separate")) ram_1 (
    .addr(Address_bus), .din(controlled_buffer_1_out), .data(ram_1_data), .str(D__MEM), .sel(1'b1),
    .clk(clock_1_out), .ld(1'b1), .clr(Reset_out));
  Button Reset (.out(Reset_out));
  assign controlled_buffer_1_out = MEM__D ? ram_1_data : 8'bz;  // Controlled_Buffer controlled_buffer_1
  // Probe on controlled_buffer_1_out
  // Probe on n0_flag_1_is_zero
  _0_Flag u_0_flag_1 (.Data(ram_1_data), .Is_zero(n0_flag_1_is_zero));
endmodule

module Output_showcase (
  input  [7:0] Data_bus,
  input  Output_flag
);

  wire clock_1_out, display_driver_1_ready, Reset_out;
  wire [3:0] display_driver_1_high_nibble, display_driver_1_low_nibble;

  Hex_Digit_Display hex_digit_display_1 (.value(display_driver_1_high_nibble));  // open: dp
  Clock clock_1 (.out(clock_1_out));
  Hex_Digit_Display hex_digit_display_2 (.value(display_driver_1_low_nibble));  // open: dp
  Display_driver display_driver_1 (
    .Data_in(Data_bus), .Reset(Reset_out), .Clock(clock_1_out), .Enable(Output_flag),
    .Ready(display_driver_1_ready), .High_nibble(display_driver_1_high_nibble),
    .Low_nibble(display_driver_1_low_nibble));
  Button Reset (.out(Reset_out));
  // Probe on display_driver_1_ready
endmodule
